# Fritzing sketch Discobrille (saved by Fritzing 0.9.3b)
breadboards: 1

parts:
  neopixel1 = Neopixel Ring 12
  Bauteil1 = Arduino Nano (Rev3.0)
  neopixel2 = Neopixel Ring 12
  KY-004_Button_Module1 = KY-004 Button Module
  Part1 = KY-002 Vibration Switch Module [package="Breakout board"]
  S1 = SPST Switch [package=switch-spst-smd-a]

nets:
  GND: neopixel1.GND, Bauteil1.GND, neopixel2.GND, KY-004_Button_Module1.-, Part1.-, S1.O
  VCC: neopixel1.VCC, Bauteil1.5V, neopixel2.VCC
  N1: neopixel1.IN, Bauteil1.D6
  N2: neopixel1.OUT, neopixel2.IN
  N3: Bauteil1.D10, Part1.S
  N4: Bauteil1.D11/MOSI, S1.P
  N5: Bauteil1.D12/MISO, KY-004_Button_Module1.S

custom parts:
  Neopixel Ring 12: Neopixel Ring x12
  KY-004 Button Module: Universal Button Module for direct use with Arduino, Raspberry & Co. Operating Voltage 3.3 V - 5 V Usual high quality and fast delivery directly from Germany by order AZ Delivery Of course, you will receive when you purchase through AZDelivery fully automatically and guarantees a Invoice incl. VAT and according to German Standards Guaranteed ROHS compliance by purchase from the German trader
  KY-002 Vibration Switch Module: Arduino Vibration Switch Module KY-002 Keyes allows detection of shock and vibration.
